# Fritzing sketch circuit (saved by Fritzing 0.9.4)
breadboards: 1

parts:
  Mod1 = KY-016 RGB Full Color LED Module [package="Breakout board"]
  SG1 = Buzzer 12mm [part_number=COM-07950 package=buzzer-12mm-ns]
  부품1 = Arduino Uno (Rev3) - ICSP
  부품2 = LCD1602-I2C
  Mod2 = KY-021 Mini Magnetic Reed Switch Module [package="Breakout board"]

nets:
  N1: Mod1.R, 부품1.D9_PWM
  N2: Mod1.G, 부품1.D10_PWM/SS
  N3: Mod1.B, 부품1.D11_PWM/MOSI
  GND: Mod1.-, SG1.2, 부품1.GND, 부품2.GND, Mod2.-
  N4: SG1.1, 부품1.D4
  N5: 부품1.A4/SDA, 부품2.SDA
  N6: 부품1.A5/SCL, 부품2.SCL
  N7: 부품1.D2, Mod2.S
  5V: 부품1.5V, 부품2.VCC, Mod2.Vin

custom parts:
  KY-016 RGB Full Color LED Module: KY-016 Arduino full color 5mm RGB LED, different colors can be obtained by mixing the three primary colors.
  Buzzer 12mm: Buzzer 12mm Spark Fun Electronics SKU : Comp-Buzzer Through hole This is a small 12mm round speaker that operates around the audible 2kHz range. You can use these speakers to create simple music or user interfaces. This is not a true piezoelectric speaker but behaves similarly. Instead of a piezoelectric crystal that vibrates with an electric current, this tiny speaker uses an electromagnet to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
  LCD1602-I2C: A standard character display, usually with 2x16 characters. Comes in many colors with LCM1602 IIC attached.
  KY-021 Mini Magnetic Reed Switch Module: KY-021 magnetic reed switch module. A reed switch is a magnetic sensor that is normally open and gets closed when exposed to a magnetic field.
